// Logisim project control_logic.circ as structural Verilog: 1 circuit, main circuit control_logic
module control_logic (
  input  [31:0] inst,
  input  BrEq,
  input  BrLt,
  output PCSel,
  output RegWEn,
  output [2:0] ImmSel,
  output BrUn,
  output ASel,
  output BSel,
  output [3:0] ALUSel,
  output MemRW,
  output [1:0] WBSel,
  output CSRSel,
  output CSRWen
);

  wire comparator_2_eq, comparator_3_eq, is_I, is_R, is_S, is_SB, is_U, is_UJ, or_2_out;
  wire [2:0] multiplexer_4_out, multiplexer_5_out, multiplexer_6_out;
  wire [3:0] multiplexer_1_out, multiplexer_2_out, multiplexer_3_out, multiplexer_7_out, multiplexer_9_out;
  wire [6:0] and_2_out, and_5_out, and_7_out, and_8_out, and_9_out, and_10_out;
  wire [6:1] and_1_out, and_3_out, and_4_out, and_6_out, or_4_out, or_5_out;

  Multiplexer #(.enable("false"), .select(3), .width(4)) multiplexer_1 (
    .in0(4'b0000), .in1(4'b0001), .in2(4'b0010), .in4(4'b0100), .in5(4'b0101), .in6(4'b0110), .in7(4'b0111),
    .out(multiplexer_1_out), .sel(inst[14:12]));  // open: in3
  Multiplexer #(.enable("false"), .select(2), .width(4)) multiplexer_2 (
    .in0(4'b0000), .in1(4'b0001), .in2(4'b0010), .in3(4'b0011), .out(multiplexer_2_out), .sel(inst[13:12]));
  or or_1 (RegWEn, is_R, is_I, is_U, is_UJ);
  Multiplexer #(.enable("false"), .select(3), .width(4)) multiplexer_3 (
    .in0(4'b0000), .in5(4'b0101), .out(multiplexer_3_out), .sel(inst[14:12]));  // open: in1, in2, in3, in4, in6, in7
  or or_2 (or_2_out, is_U, is_UJ);
  Multiplexer #(.enable("false"), .width(3)) multiplexer_4 (
    .in0(multiplexer_5_out), .in1(3'b011), .out(multiplexer_4_out), .sel(is_SB));
  Multiplexer #(.enable("false"), .width(3)) multiplexer_5 (
    .in0(multiplexer_6_out), .in1(3'b010), .out(multiplexer_5_out), .sel(is_S));
  Multiplexer #(.enable("false"), .width(3)) multiplexer_6 (
    .in0(3'b000), .in1(3'b001), .out(multiplexer_6_out), .sel(is_I));
  Multiplexer #(.enable("false"), .select(2), .width(4)) multiplexer_7 (
    .in0(multiplexer_1_out), .in1(multiplexer_2_out), .in2(multiplexer_3_out), .out(multiplexer_7_out),
    .sel(inst[26:25]));  // open: in3
  or or_3 (ASel, is_U, is_SB);
  Comparator #(.mode("unsigned"), .width(3)) comparator_1 (.a(inst[14:12]), .b(3'b101), .gt(BrUn));  // open: eq, lt
  Multiplexer #(.enable("false"), .width(3)) multiplexer_8 (
    .in0(multiplexer_4_out), .in1(3'b100), .out(ImmSel), .sel(or_2_out));
  Multiplexer #(.enable("false"), .width(4)) multiplexer_9 (
    .in0(multiplexer_7_out), .out(multiplexer_9_out), .sel(comparator_2_eq));  // open: in1
  Comparator #(.width(7)) comparator_2 (.a(7'b0110011), .b(inst[6:0]), .eq(comparator_2_eq));  // open: gt, lt
  not not_1 (BSel, is_R);
  Comparator #(.width(7)) comparator_3 (.a(7'b0110111), .b(inst[6:0]), .eq(comparator_3_eq));  // open: gt, lt
  Multiplexer #(.enable("false"), .width(4)) multiplexer_10 (
    .in0(multiplexer_9_out), .in1(4'b1110), .out(ALUSel), .sel(comparator_3_eq));
  assign {and_1_out, is_R} = inst[6:0] & 7'b0110011;  // AND_Gate and_1, 7 bits wide
  assign and_2_out = inst[6:0] & 7'b0000011;  // AND_Gate and_2, 7 bits wide
  assign {and_3_out, is_S} = inst[6:0] & 7'b0100011;  // AND_Gate and_3, 7 bits wide
  assign {and_4_out, is_SB} = inst[6:0] & 7'b1100011;  // AND_Gate and_4, 7 bits wide
  assign and_5_out = inst[6:0] & 7'b0010111;  // AND_Gate and_5, 7 bits wide
  assign {and_6_out, is_UJ} = inst[6:0] & 7'b1101111;  // AND_Gate and_6, 7 bits wide
  assign and_7_out = inst[6:0] & 7'b0010011;  // AND_Gate and_7, 7 bits wide
  assign and_8_out = inst[6:0] & 7'b1100111;  // AND_Gate and_8, 7 bits wide
  assign and_9_out = inst[6:0] & 7'b1110011;  // AND_Gate and_9, 7 bits wide
  assign and_10_out = inst[6:0] & 7'b0110111;  // AND_Gate and_10, 7 bits wide
  assign {or_4_out, is_I} = and_2_out | and_7_out | and_8_out | and_9_out;  // OR_Gate or_4, 7 bits wide
  assign {or_5_out, is_U} = and_5_out | and_10_out;  // OR_Gate or_5, 7 bits wide

  // Other names for the same wires on the sheet: opcode[6:0] = inst[6:0]; funct3[2:0] = inst[14:12];
  //   funct7[6:0] = inst[31:25]

  // Notes on the sheet:
  //   INPUTS to your circuit
  //   DON'T CHANGE THE LOCATIONS OF THE INPUTS AND OUTPUTS!
  //   OUTPUT from your circuit
endmodule
